# Fritzing sketch sustainpedaladapter (saved by Fritzing 0.9.3b)

parts:
  Pro_Micro1 = SparkFun Pro Micro
  S1 = Square Pushbutton
  R1 = Resistor [tolerance=±5% resistance=220 package="2010 [SMD]"]

nets:
  N1: Pro_Micro1.15, S1.leg1, R1.Pin_0
  N2: Pro_Micro1.VCC, S1.leg0

custom parts:
  SparkFun Pro Micro: The Pro Micro is similar to the Pro Mini except with an ATmega32U4 on board. The USB transceiver inside the 32U4 allows us to add USB connectivity on-board and do away with bulky external USB interface. Based on: https://github.com/unorthodox-engineers/unorthodox-arduino/blob/master/Unorthodox/fritzing/parts/Pro%20Micro.fzpz
